// Logisim project E8BC.circ as structural Verilog: 12 circuits, main circuit Mainboard
module ALU (
  input  [7:0] A,
  input  [1:0] FN,
  input  [7:0] B,
  input  SUB,
  input  WC,
  input  CF,
  input  [1:0] REG,
  output [7:0] OUT,
  output CY_OUT
);

  wire multiplexer_2_out;
  wire [7:0] ADD_SUB_out_6, AND_out_3, multiplexer_1_out, OR_out_3, XOR_out_3;

  Multiplexer #(.select(2), .width(8), .enable("false")) multiplexer_1 (
    .in0(B), .in1({8{1'b0}}), .in2(8'h1), .in3({8{1'b0}}), .out(multiplexer_1_out), .sel(REG));
  Multiplexer #(.enable("false")) multiplexer_2 (.in0(1'b0), .in1(CF), .out(multiplexer_2_out), .sel(WC));
  AND8b AND (.in_1(A), .in_2(multiplexer_1_out), .out_3(AND_out_3));
  OR8b OR (.in_1(A), .in_2(multiplexer_1_out), .out_3(OR_out_3));
  XOR8b XOR (.in_1(A), .in_2(multiplexer_1_out), .out_3(XOR_out_3));
  ADD_SUB_CY ADD_SUB (
    .A(A), .in_2(multiplexer_1_out), .CIN(multiplexer_2_out), .SUB(SUB), .COUT(CY_OUT), .out_6(ADD_SUB_out_6));
  Multiplexer #(.select(2), .width(8), .enable("false")) multiplexer_3 (
    .in0(AND_out_3), .in1(OR_out_3), .in2(XOR_out_3), .in3(ADD_SUB_out_6), .out(OUT), .sel(FN));

  // Notes on the sheet:
  //   A: pull=up
  //   CF: pull=up
  //   CY_OUT: pull=up
  //   OUT: pull=up
  //   REG: pull=up
  //   FN: pull=up
  //   WC: pull=up
  //   B: pull=up
  //   SUB: pull=up
endmodule

module AND8b (
  input  [7:0] in_1,
  input  [7:0] in_2,
  output [7:0] out_3
);

  and and_1 (out_3[0], in_1[0], in_2[0]);
  and and_2 (out_3[1], in_1[1], in_2[1]);
  and and_3 (out_3[2], in_1[2], in_2[2]);
  and and_4 (out_3[3], in_1[3], in_2[3]);
  and and_5 (out_3[4], in_1[4], in_2[4]);
  and and_6 (out_3[5], in_1[5], in_2[5]);
  and and_7 (out_3[6], in_1[6], in_2[6]);
  and and_8 (out_3[7], in_1[7], in_2[7]);

  // Notes on the sheet:
  //   in_2: pull=up
  //   in_1: pull=up
  //   out_3: pull=up
endmodule

module OR8b (
  input  [7:0] in_1,
  input  [7:0] in_2,
  output [7:0] out_3
);

  or or_1 (out_3[0], in_1[0], in_2[0]);
  or or_2 (out_3[1], in_1[1], in_2[1]);
  or or_3 (out_3[2], in_1[2], in_2[2]);
  or or_4 (out_3[3], in_1[3], in_2[3]);
  or or_5 (out_3[4], in_1[4], in_2[4]);
  or or_6 (out_3[5], in_1[5], in_2[5]);
  or or_7 (out_3[6], in_1[6], in_2[6]);
  or or_8 (out_3[7], in_1[7], in_2[7]);

  // Notes on the sheet:
  //   out_3: pull=up
  //   in_2: pull=up
  //   in_1: pull=up
endmodule

module XOR8b (
  input  [7:0] in_1,
  input  [7:0] in_2,
  output [7:0] out_3
);

  xor xor_1 (out_3[0], in_1[0], in_2[0]);
  xor xor_2 (out_3[1], in_1[1], in_2[1]);
  xor xor_3 (out_3[2], in_1[2], in_2[2]);
  xor xor_4 (out_3[3], in_1[3], in_2[3]);
  xor xor_5 (out_3[4], in_1[4], in_2[4]);
  xor xor_6 (out_3[5], in_1[5], in_2[5]);
  xor xor_7 (out_3[6], in_1[6], in_2[6]);
  xor xor_8 (out_3[7], in_1[7], in_2[7]);

  // Notes on the sheet:
  //   in_1: pull=up
  //   out_3: pull=up
  //   in_2: pull=up
endmodule

module ADD_SUB_CY (
  input  [7:0] A,
  input  [7:0] in_2,
  input  CIN,
  input  SUB,
  output COUT,
  output [7:0] out_6
);

  wire adder_1_cout, subtractor_1_bout;
  wire [7:0] adder_1_out, subtractor_1_out;

  Adder adder_1 (.a(A), .b(in_2), .out(adder_1_out), .cin(CIN), .cout(adder_1_cout));
  Subtractor subtractor_1 (.a(A), .b(in_2), .out(subtractor_1_out), .bin(CIN), .bout(subtractor_1_bout));
  Multiplexer #(.enable("false")) multiplexer_1 (.in0(adder_1_cout), .in1(subtractor_1_bout), .out(COUT), .sel(SUB));
  Multiplexer #(.width(8), .enable("false")) multiplexer_2 (
    .in0(adder_1_out), .in1(subtractor_1_out), .out(out_6), .sel(SUB));

  // Notes on the sheet:
  //   out_6: pull=up
  //   SUB: pull=up
  //   A: pull=up
  //   CIN: pull=up
  //   COUT: pull=up
  //   in_2: pull=up
endmodule

module Flag (
  input  [7:0] ALU_OUT,
  input  ALU_CY,
  input  CLK,
  input  CLRF,
  output [7:0] out_5
);

  wire or_1_out;
  wire [0:0] not_1_out;

  or or_1 (or_1_out, ALU_OUT[0], ALU_OUT[1], ALU_OUT[2], ALU_OUT[3], ALU_OUT[4], ALU_OUT[5], ALU_OUT[6], ALU_OUT[7]);
  Register FLAG (.D({{6{1'b0}}, ALU_CY, not_1_out[0]}), .en(1'b1), .Q(out_5), .clk(CLK), .clr(CLRF));
  not not_1 (not_1_out[0], or_1_out);

  // Notes on the sheet:
  //   CLRF: pull=up
  //   ALU_CY: pull=up
  //   out_5: pull=up
  //   CLK: pull=up
  //   ALU_OUT: pull=up
endmodule

module Controller (
  input  [7:0] IR,
  input  CLK,
  input  ZF,
  input  CLR,
  output WC,
  output [1:0] ALU_REG,
  output [1:0] ALU_FUN,
  output ALU_SUB,
  output ALU_RD,
  output A_WR,
  output A_RD,
  output B_WR,
  output B_RD,
  output COUNT_INC,
  output IR_WR,
  output LO_WR,
  output HI_WR,
  output RAM_WR,
  output RAM_RD,
  output ROM_RD,
  output LD_COUNT,
  output IO_RD,
  output IO_WR,
  output HLT
);

  wire multiplexer_1_out, not_1_out, or_1_out, Shift_counter_t1, Shift_counter_t3;
  wire [7:0] counter_1_q;
  wire [31:11] rom_1_data;

  Multiplexer #(.enable("false")) multiplexer_1 (
    .in0(1'b1), .in1(1'b0), .out(multiplexer_1_out), .sel(Shift_counter_t3));
  Counter counter_1 (
    .load(Shift_counter_t3), .D(IR), .count(multiplexer_1_out), .Q(counter_1_q), .clk(not_1_out),
    .clr(Shift_counter_t1));  // open: carry
  ROM #(.dataWidth(32)) rom_1 (
    .addr(counter_1_q),
    .data({rom_1_data[31], HLT, rom_1_data[29:22], IO_WR, IO_RD, LD_COUNT, ROM_RD, RAM_RD, RAM_WR, HI_WR, LO_WR, IR_WR, COUNT_INC, rom_1_data[11], B_RD, B_WR, A_RD, A_WR, ALU_RD, ALU_SUB, ALU_FUN, ALU_REG, WC}),
    .sel(1'b1));
  or or_1 (or_1_out, rom_1_data[31], CLR);
  not not_1 (not_1_out, CLK);
  Shift_counter Shift_counter (.CLK(CLK), .CLR(or_1_out), .T1(Shift_counter_t1), .T3(Shift_counter_t3));  // open: T2

  // Notes on the sheet:
  //   contents of rom_1 (hex, n*v repeats v):
  //   42000 1000 4*0 40200 1000 80000000 7*0 10100 80000000 44*0 40080 1000 80000000 80000000 37*0 8100
  //   80000000 6*0 4100 80000000 5*0 40000000 0 480 80000000 6*0 d8 80000000 6*0 d9 80000000 73*0 44000
  //   200100 1000 80000000 44000 100080 1000 80000000
endmodule

module Shift_counter_BAK (
  input  CLK,
  input  CLR,
  output T1,
  output T2,
  output T3,
  output T4
);

  wire d_ff_4_qn, d_ff_5_q;

  D_Flip_Flop d_ff_1 (.clk(CLK), .D(d_ff_5_q), .Q(T1), .preset(CLR), .en(1'b1));  // open: Qn, reset
  D_Flip_Flop d_ff_2 (.clk(CLK), .D(T1), .Q(T2), .en(1'b1), .reset(CLR));  // open: Qn, preset
  D_Flip_Flop d_ff_3 (.clk(CLK), .D(T2), .Q(T3), .en(1'b1), .reset(CLR));  // open: Qn, preset
  D_Flip_Flop d_ff_4 (.clk(CLK), .D(T3), .Q(T4), .Qn(d_ff_4_qn), .en(1'b1), .reset(CLR));  // open: preset
  D_Flip_Flop d_ff_5 (.D(T4), .Q(d_ff_5_q), .reset(CLR));  // open: clk, Qn, preset, en
endmodule

module Mainboard (
  input  RESET,
  input  MAN_CLK,
  input  MAN_AUTO,
  input  HALT
);

  wire CLOCK_out, microprocessor_1_hlt, microprocessor_1_io_rd, microprocessor_1_io_wr,
       microprocessor_1_ram_rd, microprocessor_1_ram_wr, microprocessor_1_rom_rd, multiplexer_1_out,
       multiplexer_2_out, or_1_out;
  wire [7:0] controlled_buffer_1_out, controlled_buffer_2_out, controlled_buffer_4_out, IN0, IN1, IN2, IN3,
       IN4, IN5, IN6, IN7, microprocessor_1_mem_out, OUT0, OUT1, OUT2, OUT3, OUT4, OUT5, OUT6, OUT7,
       pio_1_bus_out, ram_1_data, rom_1_data;
  wire [15:0] microprocessor_1_adr_ram, microprocessor_1_adr_rom;

  Clock CLOCK (.out(CLOCK_out));
  LED led_1 (.in(OUT0[7]));
  LED led_2 (.in(OUT0[5]));
  LED led_3 (.in(OUT0[6]));
  LED led_4 (.in(OUT1[6]));
  LED led_5 (.in(OUT1[5]));
  LED led_6 (.in(OUT1[7]));
  LED led_7 (.in(OUT2[5]));
  LED led_8 (.in(OUT2[6]));
  LED led_9 (.in(OUT2[7]));
  LED led_10 (.in(OUT3[6]));
  LED led_11 (.in(OUT3[7]));
  Multiplexer #(.enable("false")) multiplexer_1 (
    .in0(MAN_CLK), .in1(CLOCK_out), .out(multiplexer_1_out), .sel(MAN_AUTO));
  LED led_12 (.in(OUT0[2]));
  LED led_13 (.in(OUT0[1]));
  LED led_14 (.in(OUT0[3]));
  LED led_15 (.in(OUT0[4]));
  LED led_16 (.in(OUT1[2]));
  LED led_17 (.in(OUT1[4]));
  LED led_18 (.in(OUT1[3]));
  LED led_19 (.in(OUT1[1]));
  LED led_20 (.in(OUT2[4]));
  LED led_21 (.in(OUT2[3]));
  LED led_22 (.in(OUT2[2]));
  LED led_23 (.in(OUT2[1]));
  LED led_24 (.in(OUT3[4]));
  LED led_25 (.in(OUT3[5]));
  LED led_26 (.in(OUT3[2]));
  LED led_27 (.in(OUT3[3]));
  RAM #(.addrWidth(16), .bus("separate")) ram_1 (
    .addr(microprocessor_1_adr_ram), .din(controlled_buffer_1_out), .data(ram_1_data),
    .str(microprocessor_1_ram_wr), .sel(1'b1), .clk(multiplexer_2_out), .ld(microprocessor_1_ram_rd));  // open: clr
  ROM #(.addrWidth(16)) rom_1 (.addr(microprocessor_1_adr_rom), .data(rom_1_data), .sel(1'b1));
  Multiplexer #(.enable("false")) multiplexer_2 (
    .in0(multiplexer_1_out), .in1(1'b0), .out(multiplexer_2_out), .sel(or_1_out));
  or or_1 (or_1_out, microprocessor_1_hlt, HALT);
  LED led_28 (.in(OUT0[0]));
  LED led_29 (.in(OUT1[0]));
  LED led_30 (.in(OUT2[0]));
  LED led_31 (.in(OUT3[1]));
  LED led_32 (.in(OUT3[0]));
  assign controlled_buffer_1_out = microprocessor_1_ram_wr ? microprocessor_1_mem_out : 8'bz;  // Controlled_Buffer controlled_buffer_1
  assign controlled_buffer_2_out = microprocessor_1_ram_rd ? ram_1_data : 8'bz;  // Controlled_Buffer controlled_buffer_2
  assign controlled_buffer_2_out = microprocessor_1_rom_rd ? rom_1_data : 8'bz;  // Controlled_Buffer controlled_buffer_3
  Register register_1 (.Q(IN0));  // open: D, en, clk, clr
  Register register_2 (.Q(IN1));  // open: D, en, clk, clr
  Register register_3 (.Q(IN2));  // open: D, en, clk, clr
  Register register_4 (.Q(IN3));  // open: D, en, clk, clr
  Microprocessor microprocessor_1 (
    .CLK(multiplexer_2_out), .CLR(RESET), .ADR_RAM(microprocessor_1_adr_ram),
    .RAM_WR(microprocessor_1_ram_wr), .RAM_RD(microprocessor_1_ram_rd), .ROM_RD(microprocessor_1_rom_rd),
    .ADR_ROM(microprocessor_1_adr_rom), .MEM_OUT(microprocessor_1_mem_out), .MEM_IN(controlled_buffer_2_out),
    .HLT(microprocessor_1_hlt), .IO_RD(microprocessor_1_io_rd), .IO_WR(microprocessor_1_io_wr));
  assign controlled_buffer_4_out = microprocessor_1_io_wr ? microprocessor_1_mem_out : 8'bz;  // Controlled_Buffer controlled_buffer_4
  assign controlled_buffer_2_out = microprocessor_1_io_rd ? pio_1_bus_out : 8'bz;  // Controlled_Buffer controlled_buffer_5
  LED led_33 (.in(OUT4[5]));
  LED led_34 (.in(OUT4[4]));
  LED led_35 (.in(OUT4[6]));
  LED led_36 (.in(OUT4[7]));
  LED led_37 (.in(OUT5[6]));
  LED led_38 (.in(OUT5[4]));
  LED led_39 (.in(OUT5[7]));
  LED led_40 (.in(OUT5[5]));
  LED led_41 (.in(OUT6[7]));
  LED led_42 (.in(OUT6[5]));
  LED led_43 (.in(OUT6[6]));
  LED led_44 (.in(OUT6[4]));
  LED led_45 (.in(OUT7[6]));
  LED led_46 (.in(OUT7[5]));
  LED led_47 (.in(OUT7[7]));
  LED led_48 (.in(OUT4[1]));
  LED led_49 (.in(OUT4[0]));
  LED led_50 (.in(OUT4[2]));
  LED led_51 (.in(OUT4[3]));
  LED led_52 (.in(OUT5[0]));
  LED led_53 (.in(OUT5[1]));
  LED led_54 (.in(OUT5[2]));
  LED led_55 (.in(OUT5[3]));
  LED led_56 (.in(OUT6[1]));
  LED led_57 (.in(OUT6[2]));
  LED led_58 (.in(OUT6[0]));
  LED led_59 (.in(OUT6[3]));
  LED led_60 (.in(OUT7[1]));
  LED led_61 (.in(OUT7[4]));
  LED led_62 (.in(OUT7[3]));
  LED led_63 (.in(OUT7[2]));
  PIO pio_1 (
    .IN0(IN0), .IN1(IN1), .BUS_IN(controlled_buffer_4_out), .IN2(IN2), .IN3(IN3), .IN4(IN4), .IN5(IN5),
    .IN6(IN6), .IN7(IN7), .ADDR(microprocessor_1_adr_ram), .OUT0(OUT0), .OUT1(OUT1), .BUS_OUT(pio_1_bus_out),
    .OUT2(OUT2), .OUT3(OUT3), .OUT4(OUT4), .OUT5(OUT5), .OUT6(OUT6), .OUT7(OUT7), .CLK(multiplexer_2_out),
    .WR(microprocessor_1_io_wr), .RD(microprocessor_1_io_rd), .RST(RESET));
  LED led_64 (.in(OUT7[0]));
  Register register_5 (.Q(IN4));  // open: D, en, clk, clr
  Register register_6 (.Q(IN5));  // open: D, en, clk, clr
  Register register_7 (.Q(IN6));  // open: D, en, clk, clr
  Register register_8 (.Q(IN7));  // open: D, en, clk, clr

  // Notes on the sheet:
  //   RAM
  //   ROM
  //   contents of rom_1 (hex, n*v repeats v):
  //   d7 0 d3 0 d7 1 d3 1 d7 2 d3 2 d7 3 d3 3 d7 4 d3 4 d7 5 d3 5 d7 6 d3 6 d7 7 d3 7 76
  //   uprocessor
  //   PIO
endmodule

module Shift_counter (
  input  CLK,
  input  CLR,
  output T1,
  output T2,
  output T3
);

  wire d_ff_4_q;

  D_Flip_Flop d_ff_1 (.clk(CLK), .D(d_ff_4_q), .Q(T1), .preset(CLR), .en(1'b1));  // open: Qn, reset
  D_Flip_Flop d_ff_2 (.clk(CLK), .D(T1), .Q(T2), .en(1'b1), .reset(CLR));  // open: Qn, preset
  D_Flip_Flop d_ff_3 (.clk(CLK), .D(T2), .Q(T3), .en(1'b1), .reset(CLR));  // open: Qn, preset
  D_Flip_Flop d_ff_4 (.Q(d_ff_4_q), .reset(CLR));  // open: clk, D, Qn, preset, en
endmodule

module Microprocessor (
  input  [7:0] MEM_IN,
  input  CLK,
  input  CLR,
  output [15:0] ADR_RAM,
  output [7:0] MEM_OUT,
  output RAM_WR,
  output RAM_RD,
  output ROM_RD,
  output IO_RD,
  output [15:0] ADR_ROM,
  output IO_WR,
  output HLT
);

  wire ALU_cy_out, CF, Controller_a_rd, Controller_a_wr, Controller_alu_rd, Controller_alu_sub,
       Controller_b_rd, Controller_b_wr, Controller_wc, COUNT_INC, HI_WR, IR_WR, LD_COUNT, LO_WR, not_1_out,
       or_1_out, ZF;
  wire [1:0] Controller_alu_fun, Controller_alu_reg;
  wire [7:0] A_q, ALU_out, B_q, IR;

  Register LO (.D(MEM_IN), .en(LO_WR), .Q(ADR_RAM[7:0]), .clk(CLK), .clr(CLR));
  Register HI (.D(MEM_IN), .en(HI_WR), .Q(ADR_RAM[15:8]), .clk(CLK), .clr(CLR));
  Counter #(.width(16), .max('hffff)) COUNTER (
    .load(LD_COUNT), .D(ADR_RAM), .count(COUNT_INC), .Q(ADR_ROM), .clk(CLK), .clr(CLR));  // open: carry
  Register u_IR (.D(MEM_IN), .en(IR_WR), .Q(IR), .clk(CLK), .clr(CLR));
  assign MEM_IN = Controller_alu_rd ? ALU_out : 8'bz;  // Controlled_Buffer controlled_buffer_1
  assign MEM_IN = Controller_a_rd ? A_q : 8'bz;  // Controlled_Buffer controlled_buffer_2
  assign MEM_IN = Controller_b_rd ? B_q : 8'bz;  // Controlled_Buffer controlled_buffer_3
  Register A (.D(MEM_IN), .en(Controller_a_wr), .Q(A_q), .clk(CLK), .clr(CLR));
  Register B (.D(MEM_IN), .en(Controller_b_wr), .Q(B_q), .clk(CLK), .clr(CLR));
  ALU ALU (
    .A(A_q), .B(B_q), .WC(Controller_wc), .OUT(ALU_out), .CF(CF), .REG(Controller_alu_reg),
    .SUB(Controller_alu_sub), .FN(Controller_alu_fun), .CY_OUT(ALU_cy_out));
  or or_1 (or_1_out, ALU_out[0], ALU_out[1], ALU_out[2], ALU_out[3], ALU_out[4], ALU_out[5], ALU_out[6], ALU_out[7]);
  Controller Controller (
    .WC(Controller_wc), .ALU_REG(Controller_alu_reg), .ALU_FUN(Controller_alu_fun), .IR(IR),
    .ALU_SUB(Controller_alu_sub), .ALU_RD(Controller_alu_rd), .A_WR(Controller_a_wr), .A_RD(Controller_a_rd),
    .B_WR(Controller_b_wr), .B_RD(Controller_b_rd), .COUNT_INC(COUNT_INC), .IR_WR(IR_WR), .LO_WR(LO_WR),
    .HI_WR(HI_WR), .RAM_WR(RAM_WR), .RAM_RD(RAM_RD), .ROM_RD(ROM_RD), .LD_COUNT(LD_COUNT), .IO_RD(IO_RD),
    .IO_WR(IO_WR), .CLR(CLR), .CLK(CLK), .ZF(ZF), .HLT(HLT));
  not not_1 (not_1_out, or_1_out);
  Register #(.width(1)) u_ZF (.D(not_1_out), .en(1'b1), .Q(ZF), .clk(CLK), .clr(CLR));
  Register #(.width(1)) u_CF (.D(ALU_cy_out), .en(1'b1), .Q(CF), .clk(CLK), .clr(CLR));

  assign MEM_OUT = MEM_IN;
endmodule

module PIO (
  input  [7:0] IN0,
  input  [7:0] IN1,
  input  [7:0] BUS_IN,
  input  [7:0] IN2,
  input  [7:0] IN3,
  input  [7:0] IN4,
  input  [7:0] IN5,
  input  [7:0] IN6,
  input  [7:0] IN7,
  input  CLK,
  input  RST,
  input  [15:0] ADDR,
  input  RD,
  input  WR,
  output [7:0] OUT0,
  output [7:0] OUT1,
  output [7:0] BUS_OUT,
  output [7:0] OUT2,
  output [7:0] OUT3,
  output [7:0] OUT4,
  output [7:0] OUT5,
  output [7:0] OUT6,
  output [7:0] OUT7
);

  wire demultiplexer_2_out0, demultiplexer_2_out1, demultiplexer_2_out2, demultiplexer_2_out3,
       demultiplexer_2_out4, demultiplexer_2_out5, demultiplexer_2_out6, demultiplexer_2_out7, IN0_t, IN1_t,
       IN2_t, IN3_t, IN4_t, IN5_t, IN6_t, IN7_t, OUT0_t, OUT1_t, OUT2_t, OUT3_t, OUT4_t, OUT5_t, OUT6_t,
       OUT7_t;
  wire [7:0] controlled_buffer_1_out, controlled_buffer_2_out, controlled_buffer_3_out,
       controlled_buffer_4_out, controlled_buffer_5_out, controlled_buffer_6_out, controlled_buffer_7_out,
       controlled_buffer_8_out, demultiplexer_1_out0, demultiplexer_1_out1, demultiplexer_1_out2,
       demultiplexer_1_out3, demultiplexer_1_out4, demultiplexer_1_out5, demultiplexer_1_out6,
       demultiplexer_1_out7, register_1_q, register_2_q, register_3_q, register_4_q, register_5_q,
       register_6_q, register_7_q, register_8_q;

  Register register_1 (.D(IN0), .en(1'b1), .Q(register_1_q), .clk(CLK), .clr(RST));
  Register register_2 (.D(IN1), .en(1'b1), .Q(register_2_q), .clk(CLK), .clr(RST));
  Register register_3 (.D(IN2), .en(1'b1), .Q(register_3_q), .clk(CLK), .clr(RST));
  Register register_4 (.D(IN3), .en(1'b1), .Q(register_4_q), .clk(CLK), .clr(RST));
  Register register_5 (.D(IN4), .en(1'b1), .Q(register_5_q), .clk(CLK), .clr(RST));
  Register register_6 (.D(IN5), .en(1'b1), .Q(register_6_q), .clk(CLK), .clr(RST));
  Register register_7 (.D(IN6), .en(1'b1), .Q(register_7_q), .clk(CLK), .clr(RST));
  Register register_8 (.D(IN7), .en(1'b1), .Q(register_8_q), .clk(CLK), .clr(RST));
  Multiplexer #(.select(3), .width(8), .enable("false")) multiplexer_1 (
    .in0(register_1_q), .in1(register_2_q), .in2(register_3_q), .in3(register_4_q), .in4(register_5_q),
    .in5(register_6_q), .in6(register_7_q), .in7(register_8_q), .out(BUS_OUT), .sel(ADDR[2:0]));
  Demultiplexer #(.select(3), .width(8)) demultiplexer_1 (
    .out0(demultiplexer_1_out0), .out1(demultiplexer_1_out1), .out2(demultiplexer_1_out2),
    .out3(demultiplexer_1_out3), .out4(demultiplexer_1_out4), .out5(demultiplexer_1_out5),
    .out6(demultiplexer_1_out6), .out7(demultiplexer_1_out7), .in(BUS_IN), .sel(ADDR[2:0]));  // open: en
  assign controlled_buffer_1_out = OUT0_t ? demultiplexer_1_out0 : 8'bz;  // Controlled_Buffer controlled_buffer_1
  assign controlled_buffer_2_out = OUT1_t ? demultiplexer_1_out1 : 8'bz;  // Controlled_Buffer controlled_buffer_2
  assign controlled_buffer_3_out = OUT2_t ? demultiplexer_1_out2 : 8'bz;  // Controlled_Buffer controlled_buffer_3
  assign controlled_buffer_4_out = OUT3_t ? demultiplexer_1_out3 : 8'bz;  // Controlled_Buffer controlled_buffer_4
  assign controlled_buffer_5_out = OUT4_t ? demultiplexer_1_out4 : 8'bz;  // Controlled_Buffer controlled_buffer_5
  assign controlled_buffer_6_out = OUT5_t ? demultiplexer_1_out5 : 8'bz;  // Controlled_Buffer controlled_buffer_6
  assign controlled_buffer_7_out = OUT6_t ? demultiplexer_1_out6 : 8'bz;  // Controlled_Buffer controlled_buffer_7
  assign controlled_buffer_8_out = OUT7_t ? demultiplexer_1_out7 : 8'bz;  // Controlled_Buffer controlled_buffer_8
  Register register_9 (.D(controlled_buffer_1_out), .en(1'b1), .Q(OUT0), .clk(CLK), .clr(RST));
  Register register_10 (.D(controlled_buffer_2_out), .en(1'b1), .Q(OUT1), .clk(CLK), .clr(RST));
  Register register_11 (.D(controlled_buffer_3_out), .en(1'b1), .Q(OUT2), .clk(CLK), .clr(RST));
  Register register_12 (.D(controlled_buffer_4_out), .en(1'b1), .Q(OUT3), .clk(CLK), .clr(RST));
  Register register_13 (.D(controlled_buffer_5_out), .en(1'b1), .Q(OUT4), .clk(CLK), .clr(RST));
  Register register_14 (.D(controlled_buffer_6_out), .en(1'b1), .Q(OUT5), .clk(CLK), .clr(RST));
  Register register_15 (.D(controlled_buffer_7_out), .en(1'b1), .Q(OUT6), .clk(CLK), .clr(RST));
  Register register_16 (.D(controlled_buffer_8_out), .en(1'b1), .Q(OUT7), .clk(CLK), .clr(RST));
  Demultiplexer #(.select(3)) demultiplexer_2 (
    .out0(demultiplexer_2_out0), .out1(demultiplexer_2_out1), .out2(demultiplexer_2_out2),
    .out3(demultiplexer_2_out3), .out4(demultiplexer_2_out4), .out5(demultiplexer_2_out5),
    .out6(demultiplexer_2_out6), .out7(demultiplexer_2_out7), .in(1'b1), .sel(ADDR[2:0]));  // open: en
  and and_1 (OUT0_t, demultiplexer_2_out0, WR);
  and and_2 (OUT1_t, demultiplexer_2_out1, WR);
  and and_3 (OUT2_t, demultiplexer_2_out2, WR);
  and and_4 (OUT3_t, demultiplexer_2_out3, WR);
  and and_5 (OUT4_t, demultiplexer_2_out4, WR);
  and and_6 (OUT5_t, demultiplexer_2_out5, WR);
  and and_7 (OUT6_t, demultiplexer_2_out6, WR);
  and and_8 (OUT7_t, demultiplexer_2_out7, WR);
  and and_9 (IN0_t, demultiplexer_2_out0, RD);
  and and_10 (IN1_t, demultiplexer_2_out1, RD);
  and and_11 (IN2_t, demultiplexer_2_out2, RD);
  and and_12 (IN3_t, demultiplexer_2_out3, RD);
  and and_13 (IN4_t, demultiplexer_2_out4, RD);
  and and_14 (IN5_t, demultiplexer_2_out5, RD);
  and and_15 (IN6_t, demultiplexer_2_out6, RD);
  and and_16 (IN7_t, demultiplexer_2_out7, RD);

  // Other names for the same wires on the sheet: ADR3[2:0] = ADDR[2:0]

  // Notes on the sheet:
  //   RST: pull=up
  //   BUS_IN: pull=up
  //   OUT4: pull=up
  //   WR: pull=up
  //   OUT3: pull=up
  //   OUT2: pull=up
  //   OUT0: pull=up
  //   IN3: pull=up
  //   OUT1: pull=up
  //   IN0: pull=up
  //   IN7: pull=up
  //   ADDR: pull=up
  //   RD: pull=up
  //   IN6: pull=up
  //   OUT6: pull=up
  //   CLK: pull=up
  //   BUS_OUT: pull=up
  //   OUT7: pull=up
  //   IN1: pull=up
  //   IN4: pull=up
  //   OUT5: pull=up
  //   IN2: pull=up
  //   IN5: pull=up
endmodule
